# Fritzing sketch PlaymoDrone (saved by Fritzing 0.9.2b)
breadboards: 1

parts:
  Composant1 = Arduino Uno (Rev3) - ICSP
  IC1 = L293D [package=THT]
  M1 = DC Motor
  VCC1 = Battery block 9V
  Composant3 = SRF05 Ultrasonic Rangefinder
  C1 = Electrolytic Capacitor [capacitance=100µF package="200 mil [THT, electrolytic]"]
  Part2 = Bluetooth HC-05 Macho
  R2 = Resistor [tolerance=±5% resistance=220 package="0603 [SMD]"]
  LED3 = LED - 5mm [color="Blue (470nm)" package="5 mm [THT]"]
  J1 = Basic Servo
  LED5 = smd LED [color="White (4500K)" package="0603 [SMD]"]
  R3 = Resistor [tolerance=±5% resistance=220 package="0603 [SMD]"]
  R4 = Resistor [tolerance=±5% resistance=220 package="0603 [SMD]"]
  LED6 = smd LED [color="Red (660nm)" package="0603 [SMD]"]
  LED7 = LED - 5mm [color="Green (555nm)" package="5 mm [THT]"]  # not connected
  R5 = Resistor [tolerance=±5% resistance=220 package="0603 [SMD]"]

nets:
  N1: Composant1.D8, IC1.In_4, LED6.anode
  N2: Composant1.D10_PWM/SS, Part2.TXD
  N3: Composant1.D11_PWM/MOSI, Part2.RXD
  N4: Composant1.D12/MISO, LED5.anode
  N5: Composant1.D13/SCK, J1.pulse
  GND: Composant1.GND, IC1.0V, VCC1.-, Composant3.GND, C1.-, Part2.Key, Part2.GND, R2.Pin_1, J1.gnd, R3.Pin_1, R4.Pin_0, R5.Pin_0
  N6: Composant1.D2, Composant3.Echo
  N7: Composant1.D4, Composant3.Trig
  N8: Composant1.D6_PWM, IC1.Enable_2
  N9: Composant1.D7, IC1.In_3
  VCC: Composant1.5V, IC1.+V, Composant3.VCC, Part2.VCC, J1.vcc
  N10: IC1.+Vmotor, VCC1.+, C1.+
  N11: IC1.Out_3_(_Controlled_by_Enable_2_), M1.pin_2
  N12: IC1.Out_4_(_Controlled_by_Enable_2_), M1.pin_1
  N13: Part2.State, LED3.anode
  N14: R2.Pin_0, LED3.cathode
  N15: LED5.cathode, R3.Pin_0
  N16: R4.Pin_1, LED6.cathode

// code stored in the sketch: control-motor-arduino-l293d-chip.ino
//Code by  : Abhishek Mukhopadhyay
//Created on : May 30,2010
//Time : 11.43 am

int motorPin1 = 7;    // pin 2 on L293D
int motorPin2 = 8;    // pin 7 on L293D
int enablePin = 9;    // PWM enable & pin 1 on L293D
void setup() {
  // set all the other pins you're using as outputs:
  pinMode(motorPin1, OUTPUT);
  pinMode(motorPin2, OUTPUT);
  pinMode(enablePin, OUTPUT);
  // set enablePin high so that motor can turn on as we are not 
  //using PWM
  digitalWrite(enablePin, HIGH);
}
void loop() {
  // motor will turn on one direction:
    digitalWrite(motorPin1, LOW);   // set pin 2 on L293D low
    digitalWrite(motorPin2, HIGH);  // set pin 7 on L293D high
    delay(5000);
 //motor will turn in the opposite direction:
    digitalWrite(motorPin1, HIGH);  // set pin 2 on L293D high
    digitalWrite(motorPin2, LOW);   // set pin 7 on L293D low
    delay(5000);
 //motor will stop :
	  digitalWrite(enablePin, LOW);
    delay(5000);

}

// code stored in the sketch: PlayMoDrone.ino
//Code by  : Abhishek Mukhopadhyay and modified by Famibelle Médhi
//Created on : May 30,2010
//Time : 11.43 am

#include <Servo.h>
#include <SoftwareSerial.h>
#include <NewPing.h>

// Bluetooth done with http://www.wikidebrouillard.org/index.php/Android_et_arduino and http://eskimon.fr/2498-arduino-annexes-g-utiliser-module-bluetooth-hc-05

int motorPin1 = 7;    // pin 10 (Input A) on L293D
int motorPin2 = 8;    // pin 15 (Input B) on L293D
int enablePin = 6;    // PWM enable & pin 9 on L293D
int servoPin13 = 13;  // Servo Pin 

int Rx = 11;
int Tx = 10;
int OctetRecu = 99;

// ultra sound detector
int  trigger = 4;
int  echo = 2;
long distance = 0;
long vitesse = 0;

long temps;
long temps_recul;
int aleas; 

int Drone = 12;
boolean DroneModeActivated = true;

Servo monServo;
SoftwareSerial BTmavoieserie(Rx, Tx); // (RX, TX) (pin Rx BT, pin Tx BT)
NewPing sonar(trigger, echo, 255);

// -------------------- BEGIN SETUP --------------
void setup() {
  //on initialise le temps
  temps = millis();
  
  // set all the other pins you're using as outputs:
  pinMode(motorPin1, OUTPUT);
  pinMode(motorPin2, OUTPUT);
  pinMode(enablePin, OUTPUT);

  // set the ultrasound detector
  pinMode(trigger, OUTPUT);
  pinMode(echo, INPUT);

  // set the servo motor
  monServo.attach(servoPin13, 1000, 2000);
  monServo.write(90);

  // basic control, verifiying is all motors are up & running
  Serial.println("Initialisation du systeme");
  //digitalWrite(enablePin, HIGH);
  //moveBackward(127);
  //moveForward(127);
  //moveStop();
  turn_left();
  turn_straight();
  turn_right();
  turn_straight();

  // Ouvre la voie série avec l'ordinateur
  Serial.begin(9600);
  // Ouvre la voie série avec le module BT
  BTmavoieserie.begin(9600);

  pinMode(Drone, OUTPUT);
  }

// -------------------- END SETUP --------------

// -------------------- BEGIN FUNCTIONS --------------
void turn_left() {
  // servo turn left
  monServo.write(0);
  Serial.println("Turning left");
//  delay(1000);
}

void turn_right() {
  // servo turn right
  monServo.write(180);
  Serial.println("Turning right");
//  delay(1000);
}

void turn_straight() {
  // servo goes ahead
  monServo.write(90);
//  delay(1000);
}

void moveForward(int vitesse) {
  // motor move forward
  digitalWrite(motorPin1, HIGH); // pin 10 (Input B) on L293D
  digitalWrite(motorPin2, LOW);  // pin 15 (Input A) on L293D
  analogWrite(enablePin, vitesse);
  Serial.print(vitesse);
  Serial.println(" blocks forward");
  //delay(2000);
}

void moveBackward(int vitesse) {
  //motor moves backward
  digitalWrite(motorPin1, LOW);  // pin 10 (Input B) on L293D
  digitalWrite(motorPin2, HIGH); // pin 15 (Input A) on L293D
  analogWrite(enablePin, vitesse);
  Serial.print(vitesse);
  Serial.println(" blocks backward");
  //delay(2000);
}

void moveStop() {
  //motor stops :
  digitalWrite(motorPin1, LOW);   // pin 10 (Input B) on L293D
  digitalWrite(motorPin2, LOW);  // pin 15 (Input A) on L293D
  Serial.println("Stop");
  //delay(2000);
}

int mesure_distance() {
  long distance = 0; 
  long echoTime;

  echoTime = sonar.ping_median(5); //Do multiple pings (default=5), discard out of range pings and return median in microseconds 
  distance = sonar.convert_cm(echoTime);

  if ( distance >= 255 || distance <= 0)
  {
    Serial.println("Pas de mesure...");
    distance = 255;
  }
  else {
    Serial.print(distance);
    Serial.println(" cm de l'obstacle");
  }
  return distance;
}

void DroneMode() {
  digitalWrite(Drone, HIGH);
  int aleatoire_vitesse;
  int aleatoire_angle;
  
  distance = mesure_distance();
  vitesse = distance/1;

  if (distance<30) {
    moveBackward(127);

    if((millis() - temps_recul) > 5000) {
      aleas = random(2); // on tire un nouveau chiffre pour savoir si on tourne à gauche ou à droite.
      temps_recul = millis(); //on stocke la nouvelle heure
    }
    
    if (aleas == 1) turn_left();
    else turn_right();
  }  
  else {
    if((millis() - temps) > 2000) {
      aleatoire_vitesse = random(127,256);
      aleatoire_angle = random(181);
      moveForward(aleatoire_vitesse);
      monServo.write(aleatoire_angle);
      Serial.print(aleatoire_angle);
      Serial.println(" degrees");
      temps = millis(); //on stocke la nouvelle heure
    }
  }
}
// -------------------- END FUNCTIONS --------------

// -------------------- BEGIN LOOP --------------
void loop() {
  
  if (DroneModeActivated) digitalWrite(Drone, HIGH); else digitalWrite(Drone, LOW);
  
  if (BTmavoieserie.available()) {
    OctetRecu = BTmavoieserie.read();
    Serial.print(OctetRecu);
    Serial.println(" : par le canal BlueTooth");
    if (OctetRecu == 67) DroneModeActivated = true;
    if (OctetRecu == 68) DroneModeActivated = false;
    
    Serial.print(DroneModeActivated);
    Serial.println(" : DroneModeActivated");        

  }
  if (DroneModeActivated) {
    DroneMode();
  }
  else {
    switch (OctetRecu) {
    // source https://play.google.com/store/apps/details?id=com.inex.BlueStickControl&hl=en
    //This application use bluetooth connection in Serial Port Profile (SPP).Send hex code to robot as follows :
    //0x30 = 0d48 = '0' = Stop
    //0x38 = 0d56 = '8' = Up
    //0x32 = 0d50 = '2' = Down
    //0x34 = 0d52 = '4' = Left
    //0x36 = 0d54 = '6' = Right
    //0x41 = 0d65 = 'A' = Auto Grab
    //0x42 = 0d66 = 'B' = Auto Release
    //0x43 = 0d67 = 'C' = Grab
    //0x44 = 0d68 = 'D' = Release
    //0x45 = 0d69 = 'E' = Rotate Left
    //0x46 = 0d70 = 'F' = Rotate Right
      case 56:
        moveForward(255);
        Serial.println("en avant toute");        
        break;

      case 50:
        moveBackward(255);
        Serial.println("en arrière toute");        
        break;

      case 48:
        digitalWrite(enablePin, LOW); // le moteur passe en roue libre
        turn_straight(); // les roues se mettent droite
        break;

      case 52:
        turn_left();
        Serial.println("à gauche toute");
        break;

      case 54:
        turn_right();
        Serial.println("à droite toute");
        break;
    }
  }
}
